# Fritzing sketch LED周辺 (saved by Fritzing 0.9.3b)
breadboards: 1

parts:
  Raspberry_Pi_1 = Raspberry Pi 4 [part_number=RPI-4-b]
  LED1 = LED - 5mm [color="Red (633nm)" package="5 mm [THT]"]
  LED2 = LED - 5mm [color="Blue (505nm)" package="5 mm [THT]"]
  LED3 = LED - 5mm [color="Green (570nm)" package="5 mm [THT]"]
  LED4 = RGB LED (com. cathode, rgb) [package="5 mm [THT]"]
  OLED1 = OLED 128x64 I2C Monochrome Display
  R1 = Resistor [tolerance=±5% resistance=330 package=THT]
  R2 = Resistor [tolerance=±5% resistance=330 package=THT]
  R3 = Resistor [tolerance=±5% resistance=330 package=THT]
  R4 = Resistor [tolerance=±5% resistance=330 package=THT]
  R5 = Resistor [tolerance=±5% resistance=330 package=THT]

nets:
  N1: Raspberry_Pi_1.GPIO2, OLED1.SDA
  N2: Raspberry_Pi_1.GPIO3, OLED1.SCK
  N3: Raspberry_Pi_1.GPIO27, R5.Pin_0
  N4: Raspberry_Pi_1.GPIO22, R4.Pin_1
  N5: Raspberry_Pi_1.GPIO13, R3.Pin_0
  N6: Raspberry_Pi_1.GPIO19, R2.Pin_0
  N7: Raspberry_Pi_1.GPIO26, R1.Pin_0
  GND: Raspberry_Pi_1.GND, LED1.cathode, LED2.cathode, LED3.cathode, LED4.green_anode, OLED1.GND
  5V: Raspberry_Pi_1.5V, OLED1.VDD
  N8: LED1.anode, R1.Pin_1
  N9: LED2.anode, R3.Pin_1
  N10: LED3.anode, R2.Pin_1
  N11: LED4.red_anode, R4.Pin_0
  N12: LED4.common_cathode, R5.Pin_1

custom parts:
  Raspberry Pi 4: The RPi4, a faster version of the awesome Raspberry Pi 2 B ARM Board with 40 pin gpio. Ready for special Raspberry Pi B+ and RPi2 Hat (Hardware attached (on) top)
